// Logisim project Exercício 11.circ as structural Verilog: 1 circuit, main circuit main
module main (
  input  in_1,
  input  in_2,
  input  in_3,
  input  in_4,
  output out_5
);

  wire and_1_out, not_1_out, not_2_out, or_1_out;

  not not_1 (not_1_out, in_1);
  and and_1 (and_1_out, not_1_out, in_2, in_3);
  or or_1 (or_1_out, in_1, in_4);
  not not_2 (not_2_out, or_1_out);
  and and_2 (out_5, and_1_out, not_2_out);
endmodule
