// Logisim project Exercício 12.circ as structural Verilog: 1 circuit, main circuit main
module main (
  input  in_1,
  input  in_2,
  input  in_3,
  input  in_4,
  input  in_5,
  output out_6
);

  wire and_1_out, not_1_out, or_1_out, or_2_out;

  or or_1 (or_1_out, in_1, in_2);
  and and_1 (and_1_out, or_1_out, in_3);
  not not_1 (not_1_out, and_1_out);
  or or_2 (or_2_out, not_1_out, in_4);
  and and_2 (out_6, or_2_out, in_5);
endmodule
