// Logisim project Exercício 8.circ as structural Verilog: 1 circuit, main circuit main
module main (
  input  in_1,
  input  in_2,
  output out_3
);

  wire not_1_out, not_2_out, or_1_out, or_2_out, or_3_out;

  or or_1 (or_1_out, in_1, in_1);
  or or_2 (or_2_out, in_2, in_2);
  not not_1 (not_1_out, or_1_out);
  not not_2 (not_2_out, or_2_out);
  or or_3 (or_3_out, not_1_out, not_2_out);
  not not_3 (out_3, or_3_out);
endmodule
