// Logisim project Exercício ENAD.circ as structural Verilog: 1 circuit, main circuit main
module main (
  input  in_1,
  input  in_2,
  output out_3
);

  wire and_1_out, and_2_out, not_1_out, not_2_out;

  not not_1 (not_1_out, in_1);
  not not_2 (not_2_out, in_2);
  buf and_1 (and_1_out, not_2_out);  // AND_Gate
  and and_2 (and_2_out, not_1_out, and_1_out);
  not not_3 (out_3, and_2_out);

  // Notes on the sheet:
  //   Questão ENAD
  //   Respota D
endmodule
